// Logisim project Processor.circ as structural Verilog: 5 circuits, main circuit Processor
module Processor (
);

  wire alu_op_selector_1_e, clock_1_out;
  wire [3:0] alu_op_translator_1_h, multiplexer_5_out, sll1_1_out_2;
  wire [4:0] A_q, mips_alu_1_p6, multiplexer_1_out, multiplexer_4_out, registerfile_1_p4, Rw_q, shamt_q;
  wire [5:0] func_q, multiplexer_2_out, Op_q;
  wire [15:0] Imm_q;
  wire [26:0] A_q_2;
  wire [31:0] B_2_q, B_q, bit_extender_1_out, IF_ID_q, mips_alu_1_p5, mipsprogramrom_1_p2, multiplexer_3_out,
       pc_4_1_new, PC_q, registerfile_1_p1, registerfile_1_p7, registerfile_1_p8;

  Register #(.width(32)) PC (.D(pc_4_1_new), .Q(PC_q), .clk(clock_1_out));  // open: en, clr
  Clock clock_1 (.out(clock_1_out));
  PC_4 pc_4_1 (.Old(PC_q), .New(pc_4_1_new));
  // MIPSProgramROM mipsprogramrom_1: pin names not known; wires that end beside it: PC_q, mipsprogramrom_1_p2
  Register #(.width(32)) IF_ID (.D(mipsprogramrom_1_p2), .Q(IF_ID_q), .clk(clock_1_out));  // open: en, clr
  // Probe on IF_ID_q[20:0]
  // RegisterFile registerfile_1: pin names not known; wires that end beside it: registerfile_1_p1, clock_1_out, clock_1_out, registerfile_1_p4, IF_ID_q[25:21], IF_ID_q[20:16], registerfile_1_p7, registerfile_1_p8
  Register #(.width(32)) A (.D(registerfile_1_p7), .Q({A_q_2, A_q}), .clk(clock_1_out));  // open: en, clr
  Register #(.width(32)) B (.D(registerfile_1_p8), .Q(B_q), .clk(clock_1_out));  // open: en, clr
  Register #(.width(16)) Imm (.D(IF_ID_q[15:0]), .Q(Imm_q), .clk(clock_1_out));  // open: en, clr
  Multiplexer #(.width(5), .enable("false")) multiplexer_1 (
    .in0(IF_ID_q[15:11]), .in1(IF_ID_q[20:16]), .out(multiplexer_1_out), .sel(IF_ID_q[29]));
  Register #(.width(5)) Rw (.D(multiplexer_1_out), .Q(Rw_q), .clk(clock_1_out));  // open: en, clr
  // Probe on Op_q
  Register #(.width(6)) Op (.D(IF_ID_q[31:26]), .Q(Op_q), .clk(clock_1_out));  // open: en, clr
  Register #(.width(5)) shamt (.D(IF_ID_q[10:6]), .Q(shamt_q), .clk(clock_1_out));  // open: en, clr
  Register #(.width(6)) func (.D(IF_ID_q[5:0]), .Q(func_q), .clk(clock_1_out));  // open: en, clr
  assign bit_extender_1_out = {{16{Imm_q[15]}}, Imm_q};  // Bit_Extender bit_extender_1
  Multiplexer #(.width(6), .enable("false")) multiplexer_2 (
    .in0(func_q), .in1(Op_q), .out(multiplexer_2_out), .sel(Op_q[3]));
  Multiplexer #(.width(32), .enable("false")) multiplexer_3 (
    .in0(B_q), .in1(bit_extender_1_out), .out(multiplexer_3_out), .sel(Op_q[3]));
  // Probe on IF_ID_q[5:0]
  Multiplexer #(.width(5), .enable("false")) multiplexer_4 (
    .in0(A_q), .in1(shamt_q), .out(multiplexer_4_out), .sel(multiplexer_2_out[3]));
  SLL1 sll1_1 (.in_1(multiplexer_2_out[3:0]), .out_2(sll1_1_out_2));
  // Probe on multiplexer_2_out[3:0]
  Multiplexer #(.width(4), .enable("false")) multiplexer_5 (
    .in0(sll1_1_out_2), .in1(alu_op_translator_1_h), .out(multiplexer_5_out), .sel(alu_op_selector_1_e));
  ALU_Op_Selector alu_op_selector_1 (
    .a(multiplexer_2_out[3]), .b(multiplexer_2_out[2]), .c(multiplexer_2_out[1]), .d(multiplexer_2_out[0]),
    .e(alu_op_selector_1_e));
  // Probe on mips_alu_1_p5
  // Mips_ALU mips_alu_1: pin names not known; wires that end beside it: {A_q_2, A_q}, multiplexer_3_out, multiplexer_5_out, multiplexer_4_out, mips_alu_1_p5, mips_alu_1_p6
  ALU_Op_Translator alu_op_translator_1 (
    .a(multiplexer_2_out[3]), .b(multiplexer_2_out[2]), .c(multiplexer_2_out[1]), .d(multiplexer_2_out[0]),
    .e(alu_op_translator_1_h[3]), .f(alu_op_translator_1_h[2]), .g(alu_op_translator_1_h[1]),
    .h(alu_op_translator_1_h[0]));
  Register #(.width(32)) B_2 (.D(mips_alu_1_p5), .Q(B_2_q), .clk(clock_1_out));  // open: en, clr
  Register #(.width(5)) Rw_2 (.D(Rw_q), .Q(mips_alu_1_p6), .clk(clock_1_out));  // open: en, clr
  // Probe on multiplexer_5_out
  // Probe on sll1_1_out_2
  Register #(.width(32)) B_3 (.D(B_2_q), .Q(registerfile_1_p1), .clk(clock_1_out));  // open: en, clr
  Register #(.width(5)) Rw_3 (.D(mips_alu_1_p6), .Q(registerfile_1_p4), .clk(clock_1_out));  // open: en, clr
  // LCD_Video lcd_video_1: pin names not known
endmodule

module PC_4 (
  input  [31:0] Old,
  output [31:0] New
);

  // Incrementer incrementer_1: pin names not known; wires that end beside it: Old[31:2], New[31:2]

  assign New[1:0] = Old[1:0];
endmodule

module SLL1 (
  input  [3:0] in_1,
  output [3:0] out_2
);

  wire not_1_out;

  and and_1 (out_2[0], in_1[3], not_1_out);
  not not_1 (not_1_out, in_1[3]);

  assign out_2[3:1] = in_1[2:0];
endmodule

// Op Trans
module ALU_Op_Translator (
  input  a,
  input  b,
  input  c,
  input  d,
  output e,
  output f,
  output g,
  output h
);

  wire not_2_out;

  not not_1 (f, a);
  and and_1 (g, a, d);
  not not_2 (not_2_out, d);
  nand nand_1 (h, d, not_2_out);

  assign e = a;
endmodule

// Op Plexer
module ALU_Op_Selector (
  input  a,
  input  b,
  input  c,
  input  d,
  output e
);

  wire and_1_out, and_2_out, not_1_out, not_2_out;

  not not_1 (not_1_out, b);
  and and_1 (and_1_out, not_1_out, c, d);
  not not_2 (not_2_out, b);
  and and_2 (and_2_out, a, not_2_out, c);
  or or_1 (e, and_1_out, and_2_out);
endmodule
